# Fritzing sketch Flatpack_XY6020L_Power_Supply (saved by Fritzing 1.0.5)
breadboards: 2

parts:
  M1 = SN65HVD230 CAN Bus transciever module [package=THT]
  M2 = ESP32-S3-DevKitC-1-N8R8-v1 [part_number=ESP32-S3-DevKitC-1-N8R8-v1]
  U1 = RELAY [package=relay-g5q]
  Q1 = Basic FET P-Channel [package="TO220 [THT]"]
  D1 = Rectifier Diode [part_number=1N4001 package="300 mil [THT]"]
  R1 = Resistor [tolerance=±5% power=0.25W resistance=01k package=THT]
  R2 = Resistor [tolerance=±5% power=0.25W resistance=1k package=THT]
  R3 = Resistor [tolerance=±5% power=0.25W resistance=1k package=THT]
  U2 = Mini-360 DC-DC Buck converter [package=THT]
  Q2 = NPN-Transistor [package="TO92 [THT]"]
  Part1 = Logic Level Converter  # not connected
  IC1 = Voltage Regulator [package=to-220-alt]
  C1 = Tantalum Capacitor [capacitance=1μF voltage=35V package="100 mil [THT, tantalum]"]
  XY6020L_Real_Board1 = XY6020L - 60V 20A 1200W [mpn=XY6020L]
  Flatpack2_48/2000_HE1 = Eltek Flatpack2 48/2000 HE

nets:
  N1: M1.pin_1, M2.pin_1, M2.pin_2, U2.OUT+
  N2: M1.pin_2, M2.pin_22, M2.pin_23, M2.pin_24, M2.pin_44, Q1.source, R1.Pin_0, U2.OUT-, Q2.C
  N3: M1.pin_3, M2.pin_4
  N4: M1.pin_4, M2.pin_5
  N5: M1.pin_5, Flatpack2_48/2000_HE1.CAN_H
  N6: M1.pin_6, Flatpack2_48/2000_HE1.CAN_L
  N7: M2.pin_40, R3.Pin_1
  N8: M2.pin_41, R2.Pin_1
  N9: U1.NC, D1.cathode, U2.IN+, IC1.GND
  N10: U1.COIL1, D1.anode, Q2.E
  N11: Q1.gate, R1.Pin_1, R3.Pin_0
  N12: R2.Pin_0, Q2.B
  N13: IC1.IN, C1.-, Flatpack2_48/2000_HE1.CAN_GND
  N14: IC1.OUT, C1.+
  N15: XY6020L_Real_Board1.VIN+, Flatpack2_48/2000_HE1.DC+
  N16: XY6020L_Real_Board1.VIN-, Flatpack2_48/2000_HE1.DC-

notes:
  Fan
  12+
  GND
  12V Besleme
  (harici güç kaynağı olmalı)
  XY6020L’yi açıp kapatmak için kuru kontak uçları
  Güç Çıkışı

custom parts:
  SN65HVD230 CAN Bus transciever module: Bus Transceiver SN65HVD230 CAN Communication Module, for Arduino.
  ESP32-S3-DevKitC-1-N8R8-v1: ESP32-S3-DevKitC-1-N8R8-v1 This module is 44pins long (2x22) and 11 pins width.
  Mini-360 DC-DC Buck converter: Mini-360 DC-DC Buck converter. Tiny buck step down voltage converter, input voltage 4.75 to 23V output 1 to 17V adjustable. Available from ebay and the like.
  XY6020L - 60V 20A 1200W: Detailed XY6020L board representation based on the supplied board photograph. Includes power terminals, 4-pin UART header and ON/OFF switch connection points.
  Eltek Flatpack2 48/2000 HE: Eltek Flatpack2 48/2000 HE. Simplified Fritzing representation with AC input, CAN interface and DC output connectors.
